# Fritzing sketch auto_slider (saved by Fritzing 0.7.12b)
breadboards: 2

parts:
  Arduino1 = Arduino
  U1 = PCF8574 [package="DIP16 [THT]"]
  U2 = PCF8574 [package="DIP16 [THT]"]
  7_Segment2 = 7 Segment Display  # not connected
  7_Segment3 = 7 Segment Display
  RE1 = Rotary Encoder [package=THT]
  LED1 = LED - 3mm [color="Red (633nm)" package="3 mm [THT]"]
  LED2 = LED - 3mm [color="Red (633nm)" package="3 mm [THT]"]
  LED3 = LED - 3mm [color="Red (633nm)" package="3 mm [THT]"]
  R1 = 3.3k Ω Resistor [package=THT]
  R2 = 22 Ω Resistor [package=THT]
  J1 = Basic Servo
  S1 = Tilt Switch [package=THT]
  R3 = 22 Ω Resistor [package=THT]

nets:
  N1: Arduino1.D13, LED3.anode
  N2: Arduino1.D12, LED2.anode
  N3: Arduino1.D11, LED1.anode
  N4: Arduino1.D10, U1.P6, U2.P6
  N5: Arduino1.D9, U1.P7, U2.P7
  N6: Arduino1.D8, U1.SCL
  N7: Arduino1.D7, S1.Pin_2, R3.Pin_0
  N8: Arduino1.D6, R2.Pin_0
  N9: Arduino1.D5, J1.pulse
  N10: Arduino1.D3, RE1.EncoderPinB
  N11: Arduino1.D2, RE1.EncoderPinA
  N12: U1.P4, U2.SCL
  N13: U1.P5, U2.P5, R2.Pin_1, J1.vcc, S1.Pin_1
  N14: U1.INT, U2.INT, 7_Segment3.common_cathode#8, R1.Pin_1, J1.gnd, R3.Pin_1
  N15: U2.A0, 7_Segment3.Segment_B
  N16: U2.A1, 7_Segment3.Segment_DP
  N17: U2.A3, 7_Segment3.Segment_D
  N18: U2.P0, 7_Segment3.Segment_E
  N19: U2.P1, 7_Segment3.Segment_A#1
  N20: U2.P2, 7_Segment3.Segment_F
  N21: U2.SDA, 7_Segment3.Segment_A#10
  N22: LED1.cathode, LED2.cathode, LED3.cathode, R1.Pin_0
